# Fritzing sketch fritzing_sketch (saved by Fritzing 0.9.3b)
circuit board: 9.33863cm x 6.70622cm
breadboards: 1

parts:
  RPi = Raspberry Pi 3 [part_number=RPI-3-V1.2]
  Mot2 = Stepper Motor - Unipolar
  Mot1 = Stepper Motor - Unipolar
  MCP2 = IC, DIP package, 16 pins [chip_label=MCP3008]
  J3 = Infrared Proximity Sensor
  J4 = Infrared Proximity Sensor
  J5 = Infrared Proximity Sensor
  J6 = Infrared Proximity Sensor
  J7 = Infrared Proximity Sensor
  J8 = Infrared Proximity Sensor
  J9 = Infrared Proximity Sensor
  J10 = Infrared Proximity Sensor
  J11 = Infrared Proximity Sensor
  J12 = Infrared Proximity Sensor
  J13 = Infrared Proximity Sensor
  J14 = Infrared Proximity Sensor
  J15 = Infrared Proximity Sensor
  J16 = Infrared Proximity Sensor
  J17 = Infrared Proximity Sensor
  J18 = Infrared Proximity Sensor
  J19 = Infrared Proximity Sensor
  J20 = Infrared Proximity Sensor
  J21 = Infrared Proximity Sensor
  J22 = Infrared Proximity Sensor
  J23 = Infrared Proximity Sensor
  J24 = Infrared Proximity Sensor
  J25 = Infrared Proximity Sensor
  J26 = Infrared Proximity Sensor
  MCP3 = IC, DIP package, 16 pins [chip_label=MCP3008]
  MCP1 = IC, DIP package, 16 pins [chip_label=MCP3008]
  U1 = RELAY [package=relay-t9a-2]
  U2 = RELAY [package=relay-t9a-2]
  U3 = RELAY [package=relay-t9a-2]
  U4 = RELAY [package=relay-t9a-2]
  Elektromagnet = Solenoid
  Vcc_12V_1A = Power plug
  Mot1_TRIGGER = Square Pushbutton
  Mot2_TRIGGER = Square Pushbutton
  Pololu_A1 = Pololu A4988 [package=SO16]
  Pololu_A2 = Pololu A4988 [package=SO16]

nets:
  GND: RPi.GND, MCP2.pin9, MCP2.pin14, J3.GND, J4.GND, J5.GND, J6.GND, J7.GND, J8.GND, J9.GND, J10.GND, J11.GND, J12.GND, J13.GND, J14.GND, J15.GND, J16.GND, J17.GND, J18.GND, J19.GND, J20.GND, J21.GND, J22.GND, J23.GND, J24.GND, J25.GND, J26.GND, MCP3.pin9, MCP3.pin14, MCP1.pin9, MCP1.pin14, U1.COIL2, U1.NO, U2.COIL2, U2.NO, U3.COIL2, U4.COIL2, Pololu_A1.ENABLE, Pololu_A1.MS1, Pololu_A1.MS2, Pololu_A1.MS3, Pololu_A2.ENABLE, Pololu_A2.MS1, Pololu_A2.MS2, Pololu_A2.MS3
  N1: RPi.GPIO27, U1.NC, U2.COIL1
  N2: RPi.GPIO22, U1.COIL1, U2.NC
  VCC: RPi.3V3, MCP2.pin15, MCP2.pin16, J3.Vcc, J4.Vcc, J5.Vcc, J6.Vcc, J7.Vcc, J8.Vcc, J9.Vcc, J10.Vcc, J11.Vcc, J12.Vcc, J13.Vcc, J14.Vcc, J15.Vcc, J16.Vcc, J17.Vcc, J18.Vcc, J19.Vcc, J20.Vcc, J21.Vcc, J22.Vcc, J23.Vcc, J24.Vcc, J25.Vcc, J26.Vcc, MCP3.pin15, MCP3.pin16, MCP1.pin15, MCP1.pin16, Mot1_TRIGGER.leg1, Mot2_TRIGGER.leg1, Pololu_A1.RESET, Pololu_A1.VDD, Pololu_A2.RESET, Pololu_A2.VDD
  N3: RPi.GPIO10, MCP2.pin11, MCP3.pin11, MCP1.pin11
  N4: RPi.GPIO9, MCP2.pin12, MCP3.pin12, MCP1.pin12
  N5: RPi.GPIO11, MCP2.pin13, MCP3.pin13, MCP1.pin13
  N6: RPi.GPIO5, Pololu_A1.DIR
  N7: RPi.GPIO6, Pololu_A1.STEP
  N8: RPi.GPIO13, Pololu_A2.DIR
  N9: RPi.GPIO19, Pololu_A2.STEP
  N10: RPi.GPIO21, Mot2_TRIGGER.leg0
  N11: RPi.GPIO20, Mot1_TRIGGER.leg0
  N12: RPi.GPIO16, Pololu_A2.SLEEP
  N13: RPi.GPIO12, Pololu_A1.SLEEP
  N14: RPi.GPIO7, MCP3.pin10
  N15: RPi.GPIO25, MCP1.pin10
  N16: RPi.GPIO24, MCP2.pin10
  N17: Mot2.A, Pololu_A2.2B
  N18: Mot2.C, Pololu_A2.2A
  N19: Mot2.B, Pololu_A2.1A
  N20: Mot2.D, Pololu_A2.1B
  N21: Mot1.A, Pololu_A1.2B
  N22: Mot1.C, Pololu_A1.2A
  N23: Mot1.B, Pololu_A1.1A
  N24: Mot1.D, Pololu_A1.1B
  N25: MCP2.pin1, J12.Vout
  N26: MCP2.pin2, J17.Vout
  N27: MCP2.pin3, J16.Vout
  N28: MCP2.pin4, J13.Vout
  N29: MCP2.pin5, J11.Vout
  N30: MCP2.pin6, J15.Vout
  N31: MCP2.pin7, J14.Vout
  N32: MCP2.pin8, J18.Vout
  N33: J3.Vout, MCP1.pin8
  N34: J4.Vout, MCP1.pin7
  N35: J5.Vout, MCP1.pin6
  N36: J6.Vout, MCP1.pin5
  N37: J7.Vout, MCP1.pin4
  N38: J8.Vout, MCP1.pin3
  N39: J9.Vout, MCP1.pin2
  N40: J10.Vout, MCP1.pin1
  N41: J19.Vout, MCP3.pin7
  N42: J20.Vout, MCP3.pin4
  N43: J21.Vout, MCP3.pin3
  N44: J22.Vout, MCP3.pin6
  N45: J23.Vout, MCP3.pin1
  N46: J24.Vout, MCP3.pin8
  N47: J25.Vout, MCP3.pin2
  N48: J26.Vout, MCP3.pin5
  N49: U1.MAIN, U3.COIL1
  N50: U2.MAIN, U4.COIL1
  N51: U3.MAIN, Elektromagnet.pin1
  N52: U3.NC, U4.NC, Vcc_12V_1A.GND, Pololu_A1.GND#14, Pololu_A2.GND#14
  N53: U3.NO, U4.NO, Vcc_12V_1A.VCC, Pololu_A1.VMOT, Pololu_A2.VMOT
  N54: U4.MAIN, Elektromagnet.pin2
  N55: Pololu_A1.GND#8, Pololu_A2.GND#8

notes:
  Mot1 SLEEP - GPIO12
  Mot1 STEP - GPIO06
  Mot1 DIR - GPIO05
  Mot1 TRIG - GPIO20
  Mot2 SLEEP - GPIO16
  Mot2 STEP - GPIO19
  Mot2 DIR - GPIO13
  Mot2 TRIG - GPIO21
  CLK - SPI_CLK
  D_IN - SPI_MOSI
  D_OUT - SPI_MISO
  Mcp1_CS - GPIO25
  Mcp2_CS - GPIO24
  Mcp3_CS - GPIO07
  pinA - GPIO27
  pinB - GPIO22
